# Fritzing sketch circuit (saved by Fritzing 0.9.3b)
breadboards: 1

parts:
  IC1 = L293D [package=THT]
  JP8 = Header 6 [package=1x06_smd_straight_alt]
  Part2 = Arduino Uno (Rev3) - ICSP
  Power_plug1 = Power plug

nets:
  N1: IC1.Enable_1, IC1.Enable_2, Part2.D12/MISO
  N2: IC1.In_1, Part2.D8
  N3: IC1.Out_1_(_Controlled_by_Enable_1_), JP8.1
  GND: IC1.0V, Part2.GND, Power_plug1.GND
  N4: IC1.Out_2_(_Controlled_by_Enable_1_), JP8.2
  N5: IC1.In_2, Part2.D9_PWM
  N6: IC1.+Vmotor, Power_plug1.VCC
  N7: IC1.In_3, Part2.D10_PWM/SS
  N8: IC1.Out_3_(_Controlled_by_Enable_2_), JP8.3
  N9: IC1.+V, Part2.5V
  N10: JP8.4, Part2.D2
  N11: JP8.5, Part2.D3_PWM
  N12: JP8.6, Part2.D4

notes:
  6 pins header represents the BLDC with hall sensor connector, from left to right:
  Phase U
  Phase V
  Phase W
  Hall U
  Hall V
  Hall W
